// Digital circuit FPU.dig as structural Verilog
module FPU (
  input  [31:0] A,
  input  [31:0] B,
  input  [1:0] Sel
);

  Multiplexer #(.Bits(32), .Selector_Bits(2)) multiplexer_1 ();  // open: sel, in_0, in_1, in_2, in_3, out

  // Notes on the sheet:
  //   FPU
endmodule
