// Digital circuit exponent_difference.dig as structural Verilog
module exponent_difference (
  input  [7:0] B,
  input  [7:0] A,
  output [7:0] Q,
  output D
);

  wire comparator_1_eq, comparator_1_gt;

  Sub #(.Bits(8)) sub_1 (.a(A), .b(B), .c_i(1'b0), .s(Q));  // open: c_o
  Comparator #(.Bits(8)) comparator_1 (.a(Q), .b({8{1'b0}}), .gt(comparator_1_gt), .eq(comparator_1_eq));  // open: lt
  or or_1 (D, comparator_1_gt, comparator_1_eq);

  // Notes on the sheet:
  //   D: 1: A is greater
  //   2: B is greater
  //   Exponent Difference
endmodule
