// Digital circuit ripple-carry-adder-overflow.dig as structural Verilog
module ripple_carry_adder_overflow (
  input  [15:0] A,
  input  [15:0] B,
  input  C_in,
  output [15:0] Q,
  output C_out,
  output V
);

  wire add_1_c_o;

  Add #(.Bits(15)) add_1 (.a(A[14:0]), .b(B[14:0]), .c_i(C_in), .s(Q[14:0]), .c_o(add_1_c_o));
  Add add_2 (.a(A[15]), .b(B[15]), .c_i(add_1_c_o), .s(Q[15]), .c_o(C_out));
  xor xor_1 (V, C_out, add_1_c_o);
endmodule
